# Fritzing sketch IR Remote Control (saved by Fritzing 0.9.6b)
breadboards: 1

parts:
  U1 = ESP8266 NodeMCU LoLin module
  C2 = Electrolytic Capacitor [capacitance=100μF voltage=6.3V package="0807 [SMD, electrolytic]"]
  Q1 = Basic FET N-Channel [package="DPak [SMD]"]
  R2 = Resistor [tolerance=±5% resistance=10k package="0402 [SMD]"]
  R3 = Resistor [tolerance=±5% power=0.25 resistance=100 package=THT]
  R4 = Resistor [tolerance=±5% power=0.25 resistance=10 package=THT]
  LED1 = LED - 5mm [color="Infrared (940nm)" current=0.030 package="5 mm [THT]"]

nets:
  N1: U1.GND, C2.-, Q1.source, R2.Pin_0
  N2: U1.D7, R3.Pin_1
  N3: U1.VU, C2.+, R4.Pin_1
  N4: Q1.Gate, R2.Pin_1, R3.Pin_0
  N5: Q1.drain, LED1.cathode
  N6: R4.Pin_0, LED1.anode

custom parts:
  ESP8266 NodeMCU LoLin module: ESP8266 based NodeMCU
